# Fritzing sketch TaschenEinbau04 (saved by Fritzing 0.9.3b)

parts:
  S5 = Taiway 100-SP-X-T1 SPDT Miniature Toggle Switch [part_number=100-SP-X-T1-0-0-B1-M1 package=THT]
  S6 = Taiway 100-SP-X-T1 SPDT Miniature Toggle Switch [part_number=100-SP-X-T1-0-0-B1-M1 package=THT]  # not connected
  S7 = Taiway 100-SP-X-T1 SPDT Miniature Toggle Switch [part_number=100-SP-X-T1-0-0-B1-M1 package=THT]
  S8 = Taiway 100-SP-X-T1 SPDT Miniature Toggle Switch [part_number=100-SP-X-T1-0-0-B1-M1 package=THT]
  S9 = Taiway 100-SP-X-T1 SPDT Miniature Toggle Switch [part_number=100-SP-X-T1-0-0-B1-M1 package=THT]  # not connected
  VCC1 = 4 x AAA Battery Mount
  J1 = Piezo Speaker  # not connected
  U1 = atmega328 [package=dip]

nets:
  N1: S5.L2, U1.D7
  N2: S7.L1, U1.D2
  N3: S7.L2, VCC1.-, U1.GND
  N4: S8.L1, U1.D5_(PWM)
  N5: VCC1.+, U1.VCC, U1.AVCC
